// Logisim project 2-3not.circ as structural Verilog: 1 circuit, main circuit main
module main (
  input  IN,
  input  IN_2,
  output OUT,
  output OUT_2
);

  not not_1 (OUT_2, IN_2);
  not not_2 (OUT, IN);
endmodule
