// Logisim project 2-5nor.circ as structural Verilog: 1 circuit, main circuit main
module main (
  input  IN1,
  input  IN1_2,
  input  IN2,
  input  IN2_2,
  input  IN1_3,
  input  IN1_4,
  input  IN2_3,
  input  IN2_4,
  output OUT,
  output OUT_2,
  output OUT_3,
  output OUT_4
);

  nor nor_1 (OUT, IN1, IN2);
  nor nor_2 (OUT_4, IN1_4, IN2_4);
  nor nor_3 (OUT_2, IN1_2, IN2_2);
  nor nor_4 (OUT_3, IN1_3, IN2_3);
endmodule
