// Logisim project 2-7xnor.circ as structural Verilog: 1 circuit, main circuit main
module main (
  input  IN1,
  input  IN1_2,
  input  IN2,
  input  IN2_2,
  input  IN1_3,
  input  IN1_4,
  input  IN2_3,
  input  IN2_4,
  output OUT,
  output OUT_2,
  output OUT_3,
  output OUT_4
);

  xnor xnor_1 (OUT, IN1, IN2);
  xnor xnor_2 (OUT_3, IN1_3, IN2_3);
  xnor xnor_3 (OUT_2, IN1_2, IN2_2);
  xnor xnor_4 (OUT_4, IN1_4, IN2_4);
endmodule
