// Logisim project LAB2.4.circ as structural Verilog: 1 circuit, main circuit main
module main (
  input  E,
  input  D,
  input  D_2,
  output out_4,
  output out_5
);

  wire CLK_out;

  Clock CLK (.out(CLK_out));
  D_Flip_Flop #(.trigger("high")) d_ff_1 (
    .clk(E), .D(D), .Q(out_4), .preset(1'b0), .en(1'b1), .reset(1'b0));  // open: Qn
  D_Flip_Flop d_ff_2 (.clk(CLK_out), .D(D_2), .Q(out_5), .preset(1'b0), .en(1'b1), .reset(1'b0));  // open: Qn
endmodule
