// Logisim project adder.circ as structural Verilog: 1 circuit, main circuit main
module main (
  input  [3:0] in_1,
  input  [3:0] in_2,
  output [3:0] out_3,
  output out_4
);

  Adder #(.width(4)) adder_1 (.a(in_1), .b(in_2), .out(out_3), .cout(out_4));  // open: cin
endmodule
